# Fritzing sketch lab1 (saved by Fritzing 0.9.4)
breadboards: 1

parts:
  U1 = 7400 4 x 2 Input NAND Gate [part_number=7400 package="DIP (Dual Inline) [THT]"]
  U2 = 7400 4 x 2 Input NAND Gate [part_number=7400 package="DIP (Dual Inline) [THT]"]

nets:
  N1: U1.A1, U1.B1, U1.B4
  N2: U1.Q1, U1.Q2
  N3: U1.A2, U2.A1
  N4: U1.B2, U1.B3
  GND: U1.GND, U2.GND
  N5: U1.A3, U2.Q2, U2.A2
  N6: U1.Q3, U1.Q4
  VDD: U1.A4, U1.VDD, U2.B1, U2.VDD
  N7: U2.Q1, U2.Q3
  N8: U2.B2, U2.B3

notes:
  Input B
  Input C
  Input A
  Output of 2:1 MUX
  Output of MUX with +AC
